# Fritzing sketch strip_board_prototype (saved by Fritzing 0.9.3b)
stripboards: 1

parts:
  U1 = NodeMCU V3.0
  J1 = female pin header, 2 pins [form="♀ (female)" part_number=ALM]
  J4 = female pin header, 10 pins [form="♀ (female)"]
  J5 = female pin header, 5 pins [form="♀ (female)"]
  J6 = female pin header, 5 pins [form="♀ (female)"]
  J7 = female pin header, 10 pins [form="♀ (female)"]
  J3 = female alternating pin header, 4 pins [form="♀ (female)" part_number=VCC_SERIAL]
  J2 = female alternating pin header, 6 pins [form="♀ (female)" part_number=STEP_DIR_EN]

nets:
  N1: U1.D0, J4.pin1
  N2: U1.D1, J1.pin2, J4.pin2
  N3: U1.D2, J4.pin3
  N4: U1.D3, J4.pin4
  N5: U1.D4, J4.pin5, J2.pin2
  N6: U1.3V3, J4.pin6, J5.pin5, J6.pin1
  N7: U1.GND#6, U1.GND#13, U1.GND#16, U1.GND#33, J1.pin1, J4.pin7, J5.pin4, J6.pin4, J7.pin10, J3.pin2, J2.pin1, J2.pin3, J2.pin5
  N8: U1.D5, J4.pin8, J2.pin4
  N9: U1.D6, J4.pin9, J3.pin1
  N10: U1.D7, J4.pin10, J2.pin6
  N11: U1.D8, J5.pin1, J3.pin3
  N12: U1.RX, J5.pin2
  N13: U1.TX, J5.pin3
  N14: U1.Vin, J6.pin5, J3.pin4
  N15: U1.RST, J6.pin3
  N16: U1.EN, J6.pin2
  N17: U1.SK, J7.pin9
  N18: U1.S0, J7.pin8
  N19: U1.SC, J7.pin7
  N20: U1.S1, J7.pin6
  N21: U1.S2, J7.pin5
  N22: U1.S3, J7.pin4
  N23: U1.VU, J7.pin3
  N24: U1.GND#41, J7.pin2
  N25: U1.A0, J7.pin1

notes:
  X-ray vision, components are on the other side, strips and solder on this side
  EN-
  EN+
  DIR-
  DIR+
  STEP-
  STEP+
  ALM-
  ALM+
  VCC (5V)
  TX
  RX
  GND
  Cut this part off
  hard to follow without mirror part
  ledpin
  D0
  ALM+
  D1
  NC
  D2
  NC
  D3
  EN+
  D4
  DIR+
  D5
  Rx
  D6
  STEP+
  D7
  Tx
  D8

custom parts:
  NodeMCU V3.0: ESP8266 based NodeMCU
